# Fritzing sketch kodi (saved by Fritzing 0.9.2b)

parts:
  Raspberry_Pi1 = Raspberry Pi 2
  Q1 = NPN-Transistor [package="TO92 [THT]"]
  LED2 = LED - 3mm [color="Infrared (940nm)" package="3 mm [THT]"]
  LED3 = LED - 3mm [color="Infrared (940nm)" package="3 mm [THT]"]
  LED4 = LED - 3mm [color="Infrared (940nm)" package="3 mm [THT]"]

nets:
  N1: Raspberry_Pi1.GPIO22, Q1.B
  N2: Raspberry_Pi1.GND, Q1.E
  N3: Raspberry_Pi1.5V, LED2.cathode, LED3.cathode, LED4.cathode
  N4: Q1.C, LED2.anode, LED3.anode, LED4.anode
